# Fritzing sketch lesson 9 (saved by Fritzing 0.9.10b)

parts:
  Componente1 = Arduino Uno (Rev3)
  Part1 = KY-012 Active Buzzer Module [package="Breakout board"]

nets:
  N1: Componente1.D12/MISO, Part1.S
  N2: Componente1.GND, Part1.-

custom parts:
  KY-012 Active Buzzer Module: Active Piezoelectric Buzzer Module Keyes KY-012, it produces single-tone sound when signal is high.

// code stored in the sketch: lesson 9.ino
/* the pin of the active buzzer */
int buzzer = 12;
void setup()
{
/* initialize the buzzer pin as an output */
pinMode(buzzer, OUTPUT);
}
void loop()
{
/*define a char variable i */
  unsigned char i;
  while(1)
  {
/* output an frequency */
    for(i=0;i<80;i++)
    {
    /*When the buzzer is high, it sounds*/
      digitalWrite(buzzer,HIGH);


      delay(1); //wait for 1ms
      digitalWrite(buzzer,LOW);
      delay(1); //wait for 1ms
    }
/* output another frequency */
    for(i=0;i<100;i++)
    {
      digitalWrite(buzzer,HIGH);
      delay(2); //wait for 2ms
      digitalWrite(buzzer,LOW);
      delay(2); //wait for 2ms
    }
  }
}
