# Fritzing sketch laser (saved by Fritzing 0.9.9b)

parts:
  Componente1 = Arduino Uno (Rev3)
  Part1 = KY-008 Laser Transmitter Module [package="Breakout board"]

nets:
  N1: Componente1.D9_PWM, Part1.S
  N2: Componente1.GND, Part1.-

custom parts:
  KY-008 Laser Transmitter Module: Laser Transmitter module KY-008 for Arduino, emits a dot shaped red laser beam.
