# Fritzing sketch ejemplo1_Arduino-UNO (saved by Fritzing 0.9.9b)
breadboards: 1

parts:
  R1 = Resistor [tolerance=±5% power=0.25 resistance=270 package=THT]
  LED1 = LED - 5mm [color="Red (633nm)" current=30mA package="5 mm [THT]"]
  Componente1 = Arduino Uno (Rev3)
  R2 = Rotary Potentiometer (Small) [maximum_resistance=10kΩ package=THT]

nets:
  N1: R1.Pin_0, Componente1.D9_PWM
  N2: R1.Pin_1, LED1.anode
  GND: LED1.cathode, Componente1.GND, R2.leg2
  N3: Componente1.A3, R2.wiper
  5V: Componente1.5V, R2.leg1

notes:
  OUT: LED (D9)
  IN: POT (A3)
