# Fritzing sketch ejemplo1_tonos (saved by Fritzing 0.9.9b)
breadboards: 1

parts:
  Componente1 = Arduino Uno (Rev3)
  S1 = Pushbutton [package="[THT]"]
  S2 = Pushbutton [package="[THT]"]
  J1 = Piezo Speaker

nets:
  N1: Componente1.D8, J1.pin2
  GND: Componente1.GND, S1.Pin_1, S1.Pin_2, S2.Pin_1, S2.Pin_2, J1.pin1
  N2: Componente1.D6_PWM, S2.Pin_3, S2.Pin_4
  N3: Componente1.D7, S1.Pin_3, S1.Pin_4
