# Fritzing sketch ejemplo1_delay (saved by Fritzing 0.9.9b)

parts:
  Grove_LED_Red1 = Grove LED Red
  Componente1 = Arduino Uno (Rev3)
  Grove_Rotary_Angle_Sensor_(P)1 = Grove Rotary Angle Sensor (P)

nets:
  N1: Grove_LED_Red1.SIG, Componente1.D9_PWM
  GND: Grove_LED_Red1.GND, Componente1.GND, Grove_Rotary_Angle_Sensor_(P)1.GND
  N2: Componente1.A3, Grove_Rotary_Angle_Sensor_(P)1.SIG
  5V: Componente1.5V, Grove_Rotary_Angle_Sensor_(P)1.VCC

custom parts:
  Grove LED Red: LED red, Grove connector.
  Grove Rotary Angle Sensor (P): Rotary potentiometer, Grove connector, panel mount.
