# Fritzing sketch ESP32_nodo-office (saved by Fritzing 0.9.9b)

parts:
  U1 = ESP32S-HiLetgo [part_number=ESP32S-HiLetgo]
  Part1 = KY-019 5V Relay Module [package="Breakout board"]

nets:
  N1: U1.VIN, Part1.+
  N2: U1.GPIO5, Part1.S
  N3: U1.GND, Part1.-

custom parts:
  ESP32S-HiLetgo: HiLetgo ESP-WROOM-32 ESP32 ESP-32S Development Board 2.4GHz Dual-Mode WiFi + Bluetooth Dual Cores Microcontroller The ESP32 integrated with Antenna switches, RF Balun, power amplifiers, low-noise amplifiers, filters, and management modules, and the entire solution occupies the least area of PCB. 2.4 GHz Wi-Fi plus Bluetooth dual-mode chip, with TSMC Ultra-low power consumption 40nm technology,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
  KY-019 5V Relay Module: 5V Relay module KEYES KY-019, used to control AC circuits.
