# Fritzing sketch ESP32-thing1 (saved by Fritzing 0.9.9b)

parts:
  U1 = ESP32S-HiLetgo [part_number=ESP32S-HiLetgo]
  HC-SR04_Sensor_1 = HC-SR04 Ultrasonic Distance Sensor
  Part1 = KY-009 Full Color RGB LED SMD Module [package="Breakout board"]

nets:
  N1: U1.3.3, HC-SR04_Sensor_1.VCC
  GND: U1.GND, HC-SR04_Sensor_1.GND, Part1.-
  N2: U1.GPIO2, Part1.B
  N3: U1.GPIO0, Part1.G
  N4: U1.GPIO4, Part1.R
  N5: U1.GPIO5, HC-SR04_Sensor_1.TRIG
  N6: U1.GPIO18, HC-SR04_Sensor_1.ECHO

custom parts:
  ESP32S-HiLetgo: HiLetgo ESP-WROOM-32 ESP32 ESP-32S Development Board 2.4GHz Dual-Mode WiFi + Bluetooth Dual Cores Microcontroller The ESP32 integrated with Antenna switches, RF Balun, power amplifiers, low-noise amplifiers, filters, and management modules, and the entire solution occupies the least area of PCB. 2.4 GHz Wi-Fi plus Bluetooth dual-mode chip, with TSMC Ultra-low power consumption 40nm technology,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
  KY-009 Full Color RGB LED SMD Module: RGB full color LED Module KY-009 for Arduino, emits a range of colors by mixing red, green and blue. The amount of each primary color is adjusted using PWM.
